// Logisim project Ejercicio1.circ as structural Verilog: 1 circuit, main circuit main
module main (
  input  A,
  input  B,
  input  C,
  input  D,
  output out_5,
  output out_6,
  output out_7,
  output out_8
);

  wire and_1_out, and_2_out, and_3_out, and_4_out, and_5_out, and_6_out, and_7_out, and_8_out, and_9_out,
       and_10_out, and_11_out, and_12_out, not_1_out, not_2_out, not_3_out, not_4_out;

  not not_1 (not_1_out, A);
  not not_2 (not_2_out, B);
  not not_3 (not_3_out, C);
  not not_4 (not_4_out, D);
  and and_1 (and_1_out, A, not_2_out, not_3_out);
  and and_2 (and_2_out, not_1_out, B, not_3_out);
  and and_3 (and_3_out, not_1_out, not_2_out, C);
  and and_4 (and_4_out, B, D);
  and and_5 (and_5_out, B, C);
  and and_6 (and_6_out, C, D);
  and and_7 (and_7_out, not_2_out, not_3_out, D);
  and and_8 (and_8_out, A, B);
  and and_9 (and_9_out, not_2_out, C, not_4_out);
  and and_10 (and_10_out, not_1_out, B, not_3_out, not_4_out);
  and and_11 (and_11_out, not_2_out, D);
  and and_12 (and_12_out, A, C);
  or SA (out_5, and_1_out, and_2_out, and_3_out);
  or SD (out_6, and_4_out, and_5_out, and_6_out);
  or SC (out_7, and_7_out, and_8_out, and_9_out);
  or SB (out_8, and_10_out, and_11_out, and_12_out);
endmodule
