// Logisim project Ejercicio2-1.circ as structural Verilog
module Ej1 (
  input  [3:0] in_1,
  input  [3:0] in_2,
  output [3:0] out_3,
  output out_4
);

  wire adder_1_cout, and_1_out, or_1_out;
  wire [3:0] adder_1_out;

  Adder #(.width(4)) adder_1 (.a(in_1), .b(in_2), .out(adder_1_out), .cout(adder_1_cout));  // open: cin
  or or_1 (or_1_out, adder_1_out[1], adder_1_out[2]);
  and and_1 (and_1_out, or_1_out, adder_1_out[3]);
  or or_2 (out_4, and_1_out, adder_1_cout);
  Adder #(.width(4)) adder_2 (.a({1'b0, {2{out_4}}, 1'b0}), .b(adder_1_out), .out(out_3));  // open: cin, cout
endmodule

module Ej2 (
  input  [3:0] B,
  input  [3:0] C,
  input  [3:0] A,
  output [3:0] out_4,
  output [3:0] out_5,
  output out_6
);

  wire comparator_1_lt;

  Comparator #(.width(4), .mode("unsigned")) comparator_1 (.a(B), .b(C), .lt(comparator_1_lt));  // open: gt, eq
  Multiplexer #(.width(4), .enable("false")) multiplexer_1 (.in0(C), .in1(B), .out(out_4), .sel(comparator_1_lt));
  Ej1 ej1_1 (.in_1(out_4), .in_2(A), .out_3(out_5), .out_4(out_6));
endmodule

module Ej3 (
  input  [3:0] in_1,
  input  [3:0] in_2,
  input  [3:0] in_3,
  input  Suma_Resta,
  input  C1_C2,
  output Overflow,
  output [3:0] out_7
);

  wire adder_2_cout, and_1_out, and_2_out, xnor_1_out, xnor_2_out, xor_1_out, xor_2_out;
  wire [3:0] adder_1_out, adder_2_out, adder_3_out, adder_4_out, multiplexer_1_out, multiplexer_2_out,
       not_1_out, not_2_out;

  assign not_1_out = ~in_2;  // NOT_Gate not_1, 4 bits wide
  assign not_2_out = ~in_2;  // NOT_Gate not_2, 4 bits wide
  Multiplexer #(.width(4), .enable("false")) multiplexer_1 (
    .in0(in_2), .in1(not_1_out), .out(multiplexer_1_out), .sel(Suma_Resta));
  Adder #(.width(4)) adder_1 (.a(not_2_out), .b(4'b0001), .out(adder_1_out));  // open: cin, cout
  Adder #(.width(4)) adder_2 (.a(in_1), .b(multiplexer_1_out), .out(adder_2_out), .cout(adder_2_cout));  // open: cin
  Multiplexer #(.width(4), .enable("false")) multiplexer_2 (
    .in0(in_2), .in1(adder_1_out), .out(multiplexer_2_out), .sel(Suma_Resta));
  Adder #(.width(4)) adder_3 (.a(in_3), .b(adder_2_out), .out(adder_3_out), .cin(adder_2_cout));  // open: cout
  xnor xnor_1 (xnor_1_out, in_1[3], multiplexer_1_out[3]);
  Adder #(.width(4)) adder_4 (.a(in_1), .b(multiplexer_2_out), .out(adder_4_out));  // open: cin, cout
  and and_1 (and_1_out, xnor_1_out, xor_1_out);
  xor xor_1 (xor_1_out, multiplexer_1_out[3], adder_3_out[3]);
  xnor xnor_2 (xnor_2_out, in_1[3], multiplexer_2_out[3]);
  xor xor_2 (xor_2_out, multiplexer_2_out[3], adder_4_out[3]);
  Multiplexer #(.enable("false")) multiplexer_3 (.in0(and_1_out), .in1(and_2_out), .out(Overflow), .sel(C1_C2));
  and and_2 (and_2_out, xnor_2_out, xor_2_out);
  Multiplexer #(.width(4), .enable("false")) multiplexer_4 (
    .in0(adder_3_out), .in1(adder_4_out), .out(out_7), .sel(C1_C2));
endmodule

module Ej4 (
  input  [3:0] A,
  input  [3:0] B,
  input  [3:0] C,
  output [3:0] N,
  output [1:0] S
);

  wire comparator_1_eq, comparator_2_eq, comparator_3_eq;
  wire [3:0] multiplexer_1_out, multiplexer_2_out;

  Comparator #(.width(4)) comparator_1 (.a(A), .b(B), .eq(comparator_1_eq));  // open: gt, lt
  Comparator #(.width(4)) comparator_2 (.a(A), .b(C), .eq(comparator_2_eq));  // open: gt, lt
  Comparator #(.width(4)) comparator_3 (.a(B), .b(C), .eq(comparator_3_eq));  // open: gt, lt
  Multiplexer #(.width(4), .enable("false")) multiplexer_1 (
    .in0(A), .in1(B), .out(multiplexer_1_out), .sel(comparator_1_eq));
  Multiplexer #(.width(4), .enable("false")) multiplexer_2 (
    .in0(multiplexer_1_out), .in1(C), .out(multiplexer_2_out), .sel(comparator_3_eq));
  and and_1 (S[0], comparator_1_eq, comparator_2_eq, comparator_3_eq);
  or or_1 (S[1], comparator_1_eq, comparator_2_eq, comparator_3_eq);
  Multiplexer #(.width(4), .enable("false")) multiplexer_3 (
    .in0(4'b0000), .in1(multiplexer_2_out), .out(N), .sel(S[1]));
endmodule

module Ej6 (
  input  Presidente,
  input  Secretario,
  input  Consejero1,
  input  Consejero2,
  input  Consejero3,
  output out_6
);

  wire adder_1_cout, adder_1_out, adder_2_cout, adder_2_out, adder_3_cout, adder_5_cout, adder_5_out,
       adder_6_cout, adder_6_out, adder_7_cout, adder_7_out, adder_8_cout, adder_10_cout, comparator_1_lt,
       comparator_2_eq, comparator_2_gt, not_1_out;
  wire [2:0] adder_3_out;
  wire [3:0] adder_10_out;

  Adder #(.width(1)) adder_1 (.a(Presidente), .b(Presidente), .out(adder_1_out), .cin(Presidente), .cout(adder_1_cout));
  Adder #(.width(1)) adder_2 (.a(Consejero2), .b(Consejero3), .out(adder_2_out), .cin(Consejero1), .cout(adder_2_cout));
  Adder #(.width(1)) adder_3 (
    .a(Presidente), .b(Secretario), .out(adder_3_out[0]), .cin(adder_2_out), .cout(adder_3_cout));
  Adder #(.width(1)) adder_4 (
    .a(adder_3_cout), .b(adder_2_cout), .out(adder_3_out[1]), .cout(adder_3_out[2]));  // open: cin
  Adder #(.width(1)) adder_5 (.a(Secretario), .b(Secretario), .out(adder_5_out), .cin(Presidente), .cout(adder_5_cout));
  Adder #(.width(1)) adder_6 (
    .a(adder_2_cout), .b(adder_1_cout), .out(adder_6_out), .cin(adder_5_cout), .cout(adder_6_cout));
  Adder #(.width(1)) adder_7 (.a(adder_5_out), .b(Secretario), .out(adder_7_out), .cout(adder_7_cout));  // open: cin
  Adder #(.width(1)) adder_8 (
    .a(adder_6_out), .b(adder_10_cout), .out(adder_10_out[1]), .cin(adder_7_cout), .cout(adder_8_cout));
  Adder #(.width(1)) adder_9 (
    .a(adder_8_cout), .b(adder_6_cout), .out(adder_10_out[2]), .cout(adder_10_out[3]));  // open: cin
  Comparator #(.width(3), .mode("unsigned")) comparator_1 (
    .a(adder_3_out), .b(3'b011), .lt(comparator_1_lt));  // open: gt, eq
  Adder #(.width(1)) adder_10 (
    .a(adder_1_out), .b(adder_2_out), .out(adder_10_out[0]), .cin(adder_7_out), .cout(adder_10_cout));
  not not_1 (not_1_out, comparator_1_lt);
  Comparator #(.width(4), .mode("unsigned")) comparator_2 (
    .a(adder_10_out), .b(4'b0101), .gt(comparator_2_gt), .eq(comparator_2_eq));  // open: lt
  Multiplexer #(.enable("false")) multiplexer_1 (
    .in0(comparator_2_gt), .in1(not_1_out), .out(out_6), .sel(comparator_2_eq));
endmodule

module Ej6b (
  input  Presidente,
  input  Secretario,
  input  Consejero1,
  input  Consejero2,
  input  Consejero3,
  output out_6
);

  wire comparator_1_eq, comparator_1_gt, comparator_2_lt, not_1_out;
  wire [2:0] ej6_2_1_out_6;
  wire [3:0] ej6_1_1_out_6;

  Ej6_1 ej6_1_1 (
    .Presidente(Presidente), .Secretario(Secretario), .Consejero1(Consejero1), .Consejero2(Consejero2),
    .Consejero3(Consejero3), .out_6(ej6_1_1_out_6));
  Ej6_2 ej6_2_1 (
    .Presidente(Presidente), .Secretario(Secretario), .Consejero1(Consejero1), .Consejero2(Consejero2),
    .Consejero3(Consejero3), .out_6(ej6_2_1_out_6));
  Comparator #(.width(4), .mode("unsigned")) comparator_1 (
    .a(ej6_1_1_out_6), .b(4'b0101), .gt(comparator_1_gt), .eq(comparator_1_eq));  // open: lt
  Comparator #(.width(3), .mode("unsigned")) comparator_2 (
    .a(ej6_2_1_out_6), .b(3'b011), .lt(comparator_2_lt));  // open: gt, eq
  not not_1 (not_1_out, comparator_2_lt);
  Multiplexer #(.enable("false")) multiplexer_1 (
    .in0(comparator_1_gt), .in1(not_1_out), .out(out_6), .sel(comparator_1_eq));
endmodule

module Ej6_1 (
  input  Presidente,
  input  Secretario,
  input  Consejero1,
  input  Consejero2,
  input  Consejero3,
  output [3:0] out_6
);

  wire ej6_3_1_out_4, ej6_3_1_out_5, ej6_3_2_out_4, ej6_3_2_out_5, ej6_3_3_out_4, ej6_3_3_out_5,
       ej6_3_4_out_4, ej6_3_4_out_5, ej6_3_5_out_4, ej6_3_5_out_5, ej6_3_6_out_5, ej6_3_8_out_5;

  Ej6_3 ej6_3_1 (.in_2(Presidente), .in_3(Presidente), .in_1(Presidente), .out_5(ej6_3_1_out_5), .out_4(ej6_3_1_out_4));
  Ej6_3 ej6_3_2 (.in_2(Consejero2), .in_3(Consejero3), .in_1(Consejero1), .out_5(ej6_3_2_out_5), .out_4(ej6_3_2_out_4));
  Ej6_3 ej6_3_3 (.in_2(Secretario), .in_3(Secretario), .in_1(Presidente), .out_5(ej6_3_3_out_5), .out_4(ej6_3_3_out_4));
  Ej6_3 ej6_3_4 (
    .in_2(ej6_3_2_out_5), .in_3(ej6_3_1_out_5), .in_1(ej6_3_3_out_5), .out_5(ej6_3_4_out_5),
    .out_4(ej6_3_4_out_4));
  Ej6_3 ej6_3_5 (.in_2(ej6_3_3_out_4), .in_3(Secretario), .in_1(1'b0), .out_5(ej6_3_5_out_5), .out_4(ej6_3_5_out_4));
  Ej6_3 ej6_3_6 (
    .in_2(ej6_3_4_out_4), .in_3(ej6_3_8_out_5), .in_1(ej6_3_5_out_5), .out_5(ej6_3_6_out_5), .out_4(out_6[1]));
  Ej6_3 ej6_3_7 (.in_2(ej6_3_6_out_5), .in_3(ej6_3_4_out_5), .in_1(1'b0), .out_5(out_6[3]), .out_4(out_6[2]));
  Ej6_3 ej6_3_8 (
    .in_2(ej6_3_1_out_4), .in_3(ej6_3_2_out_4), .in_1(ej6_3_5_out_4), .out_5(ej6_3_8_out_5), .out_4(out_6[0]));
endmodule

module Ej6_2 (
  input  Presidente,
  input  Secretario,
  input  Consejero1,
  input  Consejero2,
  input  Consejero3,
  output [2:0] out_6
);

  wire ej6_3_1_out_4, ej6_3_1_out_5, ej6_3_2_out_5;

  Ej6_3 ej6_3_1 (.in_2(Consejero2), .in_3(Consejero3), .in_1(Consejero1), .out_5(ej6_3_1_out_5), .out_4(ej6_3_1_out_4));
  Ej6_3 ej6_3_2 (.in_2(Presidente), .in_3(Secretario), .in_1(ej6_3_1_out_4), .out_5(ej6_3_2_out_5), .out_4(out_6[0]));
  Ej6_3 ej6_3_3 (.in_2(ej6_3_2_out_5), .in_3(ej6_3_1_out_5), .in_1(1'b0), .out_5(out_6[2]), .out_4(out_6[1]));
endmodule

module Ej6_3 (
  input  in_1,
  input  in_2,
  input  in_3,
  output out_4,
  output out_5
);

  wire and_1_out, and_2_out, or_1_out, xor_1_out;

  and and_1 (and_1_out, in_2, in_3);
  or or_1 (or_1_out, in_2, in_3);
  xor xor_1 (xor_1_out, in_2, in_3);
  and and_2 (and_2_out, or_1_out, in_1);
  or or_2 (out_5, and_1_out, and_2_out);
  xor xor_2 (out_4, xor_1_out, in_1);
endmodule
