// Logisim project Ejercicio2.circ as structural Verilog: 3 circuits, main circuit main
module main (
  input  A,
  input  B,
  input  C,
  output out_4,
  output out_5,
  output out_6,
  output out_7
);

  wire and_1_out, and_2_out, nand_1_out, nand_2_out, nor_1_out, nor_2_out, or_1_out;

  or or_1 (or_1_out, B, C);
  and and_1 (and_1_out, A, B);
  and and_2 (and_2_out, A, C);
  nor nor_1 (nor_1_out, A, A);
  nor nor_2 (nor_2_out, B, C);
  nand nand_1 (nand_1_out, A, B);
  nand nand_2 (nand_2_out, A, C);
  and and_3 (out_4, A, or_1_out);
  or or_2 (out_5, and_1_out, and_2_out);
  nor nor_3 (out_6, nor_1_out, nor_2_out);
  nand nand_3 (out_7, nand_1_out, nand_2_out);
endmodule

module UsarModulo (
  input  A3,
  input  A2,
  input  A1,
  input  B3,
  input  B2,
  input  B1,
  output out_7
);

  wire auxiliar_1_out_4, auxiliar_2_out_4;

  Auxiliar auxiliar_1 (.A(A1), .B(A2), .C(A3), .out_4(auxiliar_1_out_4));
  Auxiliar auxiliar_2 (.A(B1), .B(B2), .C(B3), .out_4(auxiliar_2_out_4));
  or or_1 (out_7, auxiliar_1_out_4, auxiliar_2_out_4);
endmodule

module Auxiliar (
  input  A,
  input  B,
  input  C,
  output out_4
);

  wire and_1_out, and_2_out;

  and and_1 (and_1_out, A, B);
  and and_2 (and_2_out, A, C);
  or or_1 (out_4, and_1_out, and_2_out);
endmodule
