// Logisim project Ejercicio4.circ as structural Verilog: 1 circuit, main circuit main
module main (
  input  S1,
  input  S2,
  input  EM,
  input  S1_2,
  input  S2_2,
  input  EM_2,
  output Error,
  output Error_2,
  output M1,
  output M1_2,
  output M2,
  output M2_2
);

  wire nor_1_out, nor_2_out, nor_3_out;

  and and_1 (Error_2, ~S1, S2, EM);  // AND_Gate
  and and_2 (M1, S1, EM);
  and and_3 (M2, S2, EM);
  nor nor_1 (nor_1_out, S1_2, S1_2);
  nor nor_2 (nor_2_out, EM_2, EM_2);
  nor nor_3 (nor_3_out, S2_2, S2_2);
  nor nor_4 (Error, S1_2, nor_3_out, nor_2_out);
  nor nor_5 (M1_2, nor_1_out, nor_2_out);
  nor nor_6 (M2_2, nor_2_out, nor_3_out);
endmodule
