// Logisim project Ejercicio5.circ as structural Verilog: 1 circuit, main circuit main
module main (
  input  Ahorro,
  input  Dia,
  input  t1,
  input  t0,
  output Enfriar,
  output Calentar
);

  wire and_1_out, and_2_out, or_1_out;

  and and_1 (and_1_out, ~Ahorro, Dia, t1);  // AND_Gate
  and and_2 (and_2_out, t1, ~t0);  // AND_Gate
  or or_1 (or_1_out, ~Ahorro, Dia);  // OR_Gate
  or or_2 (Enfriar, and_1_out, and_2_out);
  and and_3 (Calentar, ~t0, ~t1, or_1_out);  // AND_Gate
endmodule
