// Logisim project EjercicioOpcional.circ as structural Verilog: 1 circuit, main circuit main
module main (
  input  P1,
  input  P2,
  input  M3,
  input  P4,
  input  M5,
  input  M6,
  input  M7,
  output ERROR,
  output ERROR_2,
  output ERROR_3,
  output [6:0] out_11
);

  wire and_1_out, and_2_out, and_3_out, and_4_out, and_5_out, and_6_out, and_7_out, and_8_out, and_9_out,
       and_10_out, not_1_out, not_2_out, not_3_out, not_4_out;

  not not_1 (not_1_out, M3);
  not not_2 (not_2_out, M5);
  not not_3 (not_3_out, M6);
  not not_4 (not_4_out, M7);
  and and_1 (and_1_out, M5, not_4_out);
  and and_2 (and_2_out, M3, not_4_out);
  and and_3 (and_3_out, not_1_out, not_2_out, M7);
  and and_4 (and_4_out, M3, not_4_out);
  and and_5 (and_5_out, M6, not_4_out);
  and and_6 (and_6_out, not_1_out, not_3_out, M7);
  and and_7 (and_7_out, not_2_out, not_3_out, M7);
  and and_8 (and_8_out, not_2_out, M6, not_4_out);
  and and_9 (and_9_out, M5, M6, M7);
  and and_10 (and_10_out, M5, not_3_out, not_4_out);
  or or_1 (out_11[6], and_1_out, and_2_out, and_3_out);
  or or_2 (out_11[5], and_4_out, and_5_out, and_6_out);
  or or_3 (out_11[3], and_7_out, and_8_out, and_9_out, and_10_out);
  xor xor_1 (ERROR, P1, out_11[6]);
  xor xor_2 (ERROR_2, P2, out_11[5]);
  xor xor_3 (ERROR_3, and_7_out, P4);

  assign {out_11[4], out_11[2:0]} = {M3, M5, M6, M7};
endmodule
