// Logisim project Examen22_4.circ as structural Verilog: 1 circuit, main circuit main
module main (
  input  [3:0] in_1,
  input  [3:0] in_2,
  input  [3:0] in_3,
  input  [3:0] in_4,
  output out_5,
  output [3:0] out_6
);

  wire clock_1_out, comparator_1_lt, t_ff_1_q, xor_1_out, xor_2_out;
  wire [3:0] adder_1_out, multiplexer_1_out;

  xor xor_1 (xor_1_out, in_3[3], in_4[3]);
  Comparator #(.width(4), .mode("unsigned")) comparator_1 (.a(in_3), .b(in_4), .lt(comparator_1_lt));  // open: gt, eq
  Multiplexer #(.width(4), .enable("false")) multiplexer_1 (
    .in0(in_3), .in1(in_4), .out(multiplexer_1_out), .sel(xor_2_out));
  xor xor_2 (xor_2_out, comparator_1_lt, xor_1_out);
  T_Flip_Flop t_ff_1 (.clk(clock_1_out), .T(1'b1), .Q(t_ff_1_q));  // open: Qn, preset, reset, en
  Clock clock_1 (.out(clock_1_out));
  Adder #(.width(4)) adder_1 (.a(multiplexer_1_out), .b(in_2), .out(adder_1_out));  // open: cin, cout
  and and_1 (out_5, ~adder_1_out[0], ~adder_1_out[1], ~adder_1_out[2], adder_1_out[3], t_ff_1_q);  // AND_Gate
  Multiplexer #(.width(4), .enable("false")) multiplexer_2 (.in0(in_1), .in1(adder_1_out), .out(out_6), .sel(t_ff_1_q));
endmodule
